// Logisim project CPU.circ as structural Verilog: 12 circuits, main circuit main
module main (
);

  wire clk, ld_str_chip_1_lda, ld_str_chip_1_sel, ld_str_chip_1_str, R0, rmctl, rwctl, wmctl;
  wire [1:0] pcctl, rdctl;
  wire [2:0] rinctl;
  wire [3:0] idec_1_op, rdctl_chip_1_rdctl_out, RsX_ctl;
  wire [7:0] Adress, DM_Out, Out_ULA, PC_Out, rinclt_chip_1_rinctl_out_2, RX_out, RY_out;
  wire [11:0] rom_1_data;
  wire [11:8] IR_Out;

  IDEC idec_1 (.\INSTRUÇÃO ({IR_Out, Adress}), .Op(idec_1_op));
  RsX_ctl rsx_ctl_1 (.RsX(Adress[7:4]), .Op(IR_Out), .RsX_out(RsX_ctl));
  PC pc_1 (.PC_Adress(Adress), .pcctl(pcctl), .PC_clk(clk), .PC_Out(PC_Out));
  CTLU ctlu_1 (
    .Op(idec_1_op), .R0(R0), .rmctl(rmctl), .rwctl(rwctl), .rinctl(rinctl), .rdctl(rdctl), .wmctl(wmctl),
    .pcctl(pcctl));
  ROM #(.dataWidth(12)) rom_1 (.addr(PC_Out), .data(rom_1_data));  // open: sel
  IR ir_1 (.IR_In(rom_1_data), .clk(clk), .IR_Out({IR_Out, Adress}));
  Clock clock_1 (.out(clk));
  rdctl_chip rdctl_chip_1 (.RsX(Adress[7:4]), .rdctl(rdctl), .rdctl_out(rdctl_chip_1_rdctl_out));
  rinclt_chip rinclt_chip_1 (
    .ula_out(Out_ULA), .dm_out(DM_Out), .adress(Adress), .rinctl_out(RY_out), .pc_out(PC_Out),
    .rinctl(rinctl), .rinctl_out_2(rinclt_chip_1_rinctl_out_2));
  Registrador registrador_1 (
    .RsX(RsX_ctl), .RsY(Adress[3:0]), .Rd(rdctl_chip_1_rdctl_out), .Rin(rinclt_chip_1_rinctl_out_2),
    .rwctl(rwctl), .R0(R0), .Rx(RX_out), .Ry(RY_out), .clk(clk));
  \Unidade_Lógica_Aritimética  \unidade_lógica_aritimética_1  (
    .Ix(RX_out), .Iy(RY_out), .Op(IR_Out), .ula_out(Out_ULA));
  RAM #(.bus("separate")) ram_1 (
    .addr(Adress), .din(RX_out), .data(DM_Out), .str(ld_str_chip_1_str), .sel(ld_str_chip_1_sel), .clk(clk),
    .ld(ld_str_chip_1_lda));  // open: clr
  ld_str_chip ld_str_chip_1 (
    .wmctl(rmctl), .Op(IR_Out), .LDA(ld_str_chip_1_lda), .STR(ld_str_chip_1_str), .sel(ld_str_chip_1_sel));

  // Other names for the same wires on the sheet: IR_Out[7:0] = Adress; RsY[3:0] = Adress[3:0]; RsX[3:0] = Adress[7:4];
  //   Op[3:0] = IR_Out

  // Notes on the sheet:
  //   ROM - Instruction Memory
  //   contents of rom_1 (hex, n*v repeats v):
  //   b00 c00 d10 b0a d20 b01 d30 812 200 e0e 331 d10 b01 e07 d01 c00 f00
  //   UFBa - Universidade Federal da Bahia
  //   Gustavo de Oliveira Ferreia
  //   gust.oliveira.ferreira@gmail.com
  //   FINAL ARQUITETURA - ARQ38
  //   Fase 3: Criação do CPU e união com memórias
  //   RAM - Data Memory
endmodule

// REG
module Registrador (
  input  [3:0] RsX,
  input  [3:0] RsY,
  input  [3:0] Rd,
  input  [7:0] Rin,
  input  rwctl,
  input  clk,
  output R0,
  output [7:0] Rx,
  output [7:0] Ry
);

  wire comparator_1_eq, demultiplexer_1_out0, demultiplexer_1_out1, demultiplexer_1_out2,
       demultiplexer_1_out3, demultiplexer_1_out4, demultiplexer_1_out5, demultiplexer_1_out6,
       demultiplexer_1_out7, demultiplexer_1_out8, demultiplexer_1_out9, demultiplexer_1_out10,
       demultiplexer_1_out11, demultiplexer_1_out12, demultiplexer_1_out13, demultiplexer_1_out14,
       demultiplexer_1_out15, not_1_out;
  wire [7:0] register_1_q, register_2_q, register_3_q, register_4_q, register_5_q, register_6_q,
       register_7_q, register_8_q, register_9_q, register_10_q, register_11_q, register_12_q, register_13_q,
       register_14_q, register_15_q, register_16_q;

  not not_1 (not_1_out, rwctl);
  Demultiplexer #(.select(4), .enable("false")) demultiplexer_1 (
    .out0(demultiplexer_1_out0), .out1(demultiplexer_1_out1), .out2(demultiplexer_1_out2),
    .out3(demultiplexer_1_out3), .out4(demultiplexer_1_out4), .out5(demultiplexer_1_out5),
    .out6(demultiplexer_1_out6), .out7(demultiplexer_1_out7), .out8(demultiplexer_1_out8),
    .out9(demultiplexer_1_out9), .out10(demultiplexer_1_out10), .out11(demultiplexer_1_out11),
    .out12(demultiplexer_1_out12), .out13(demultiplexer_1_out13), .out14(demultiplexer_1_out14),
    .out15(demultiplexer_1_out15), .in(not_1_out), .sel(Rd));
  Register register_1 (.D(Rin), .en(demultiplexer_1_out0), .Q(register_1_q), .clk(clk));  // open: clr
  Register register_2 (.D(Rin), .en(demultiplexer_1_out1), .Q(register_2_q), .clk(clk));  // open: clr
  Register register_3 (.D(Rin), .en(demultiplexer_1_out2), .Q(register_3_q), .clk(clk));  // open: clr
  Register register_4 (.D(Rin), .en(demultiplexer_1_out3), .Q(register_4_q), .clk(clk));  // open: clr
  Register register_5 (.D(Rin), .en(demultiplexer_1_out4), .Q(register_5_q), .clk(clk));  // open: clr
  Register register_6 (.D(Rin), .en(demultiplexer_1_out5), .Q(register_6_q), .clk(clk));  // open: clr
  Register register_7 (.D(Rin), .en(demultiplexer_1_out6), .Q(register_7_q), .clk(clk));  // open: clr
  Register register_8 (.D(Rin), .en(demultiplexer_1_out7), .Q(register_8_q), .clk(clk));  // open: clr
  Register register_9 (.D(Rin), .en(demultiplexer_1_out8), .Q(register_9_q), .clk(clk));  // open: clr
  Register register_10 (.D(Rin), .en(demultiplexer_1_out9), .Q(register_10_q), .clk(clk));  // open: clr
  Register register_11 (.D(Rin), .en(demultiplexer_1_out10), .Q(register_11_q), .clk(clk));  // open: clr
  Register register_12 (.D(Rin), .en(demultiplexer_1_out11), .Q(register_12_q), .clk(clk));  // open: clr
  Register register_13 (.D(Rin), .en(demultiplexer_1_out12), .Q(register_13_q), .clk(clk));  // open: clr
  Register register_14 (.D(Rin), .en(demultiplexer_1_out13), .Q(register_14_q), .clk(clk));  // open: clr
  Register register_15 (.D(Rin), .en(demultiplexer_1_out14), .Q(register_15_q), .clk(clk));  // open: clr
  Register register_16 (.D(Rin), .en(demultiplexer_1_out15), .Q(register_16_q), .clk(clk));  // open: clr
  Comparator comparator_1 (.a({8{1'b0}}), .b(register_1_q), .eq(comparator_1_eq));  // open: gt, lt
  not not_2 (R0, comparator_1_eq);
  Multiplexer #(.select(4), .width(8), .enable("false")) multiplexer_1 (
    .in0(register_1_q), .in1(register_2_q), .in2(register_3_q), .in3(register_4_q), .in4(register_5_q),
    .in5(register_6_q), .in6(register_7_q), .in7(register_8_q), .in8(register_9_q), .in9(register_10_q),
    .in10(register_11_q), .in11(register_12_q), .in12(register_13_q), .in13(register_14_q),
    .in14(register_15_q), .in15(register_16_q), .out(Rx), .sel(RsX));
  Multiplexer #(.select(4), .width(8), .enable("false")) multiplexer_2 (
    .in0(register_1_q), .in1(register_2_q), .in2(register_3_q), .in3(register_4_q), .in4(register_5_q),
    .in5(register_6_q), .in6(register_7_q), .in7(register_8_q), .in8(register_9_q), .in9(register_10_q),
    .in10(register_11_q), .in11(register_12_q), .in12(register_13_q), .in13(register_14_q),
    .in14(register_15_q), .in15(register_16_q), .out(Ry), .sel(RsY));

  // Other names for the same wires on the sheet: Rs1[3:0] = RsX; Rs2[3:0] = RsY

  // Notes on the sheet:
  //   Entradas REGs
  //   UFBa - Universidade Federal da Bahia
  //   Gustavo de Oliveira Ferreia
  //   gust.oliveira.ferreira@gmail.com
  //   BANCO DE REGISTRADORES - REGS
  //   Fase 2.1: Implementação do REGs
  //   Saidas REGs
endmodule

// ULA
module \Unidade_Lógica_Aritimética  (
  input  [7:0] Ix,
  input  [7:0] Iy,
  input  [3:0] Op,
  output [7:0] ula_out
);

  wire comparator_1_eq, comparator_2_eq, comparator_3_lt, comparator_4_eq, comparator_4_lt, or_2_out;
  wire [7:0] adder_1_out, and_1_out, bit_extender_1_out, bit_extender_2_out, bit_extender_3_out,
       bit_extender_4_out, divider_1_out, multiplier_1_out, or_1_out, subtractor_1_out;

  assign and_1_out = Ix & Iy;  // AND_Gate and_1, 8 bits wide
  assign or_1_out = Ix | Iy;  // OR_Gate or_1, 8 bits wide
  Comparator comparator_1 (.a({8{1'b0}}), .b(Iy), .eq(comparator_1_eq));  // open: gt, lt
  Adder adder_1 (.a(Ix), .b(Iy), .out(adder_1_out));  // open: cin, cout
  Subtractor subtractor_1 (.a(Ix), .b(Iy), .out(subtractor_1_out));  // open: bin, bout
  Multiplier multiplier_1 (.a(Ix), .b(Iy), .out(multiplier_1_out));  // open: cin, cout
  Divider divider_1 (.a(Ix), .b(Iy), .out(divider_1_out));  // open: upper, rem
  Comparator comparator_2 (.a(Ix), .b(Iy), .eq(comparator_2_eq));  // open: gt, lt
  Comparator comparator_3 (.a(Ix), .b(Iy), .lt(comparator_3_lt));  // open: gt, eq
  Comparator comparator_4 (.a(Ix), .b(Iy), .eq(comparator_4_eq), .lt(comparator_4_lt));  // open: gt
  assign bit_extender_1_out = {{7{1'b0}}, comparator_1_eq};  // Bit_Extender bit_extender_1
  or or_2 (or_2_out, comparator_4_eq, comparator_4_lt);
  assign bit_extender_2_out = {{7{1'b0}}, comparator_2_eq};  // Bit_Extender bit_extender_2
  assign bit_extender_3_out = {{7{1'b0}}, comparator_3_lt};  // Bit_Extender bit_extender_3
  assign bit_extender_4_out = {{7{1'b0}}, or_2_out};  // Bit_Extender bit_extender_4
  Multiplexer #(.select(4), .width(8), .enable("false")) multiplexer_1 (
    .in0(and_1_out), .in1(or_1_out), .in2(bit_extender_1_out), .in3(adder_1_out), .in4(subtractor_1_out),
    .in5(multiplier_1_out), .in6(divider_1_out), .in7(bit_extender_2_out), .in8(bit_extender_3_out),
    .in9(bit_extender_4_out), .out(ula_out), .sel(Op));  // open: in10, in11, in12, in13, in14, in15

  // Notes on the sheet:
  //   Entradas ULA
  //   UFBa - Universidade Federal da Bahia
  //   Gustavo de Oliveira Ferreia
  //   gust.oliveira.ferreira@gmail.com
  //   UNIDADE LÓGICA ARITIMÉTICA - ULA
  //   Fase 1: Implementação da ULA 
  //   Saída ULA
endmodule

module REG_ULA (
  input  [3:0] RsX,
  input  [1:0] rdctl,
  input  [3:0] RsY,
  input  rwctl,
  input  [2:0] rinctl,
  output [7:0] out_6,
  output [7:0] out_7,
  output [7:0] ula_out
);

  wire clock_1_out, R0;
  wire [3:0] multiplexer_1_out, RsX_t, ula_op;
  wire [7:0] multiplexer_2_out;

  Multiplexer #(.select(2), .width(4), .enable("false")) multiplexer_1 (
    .in0(4'b0000), .in1(4'b1111), .in2(RsX_t), .out(multiplexer_1_out), .sel(rdctl));  // open: in3
  Multiplexer #(.select(3), .width(8), .enable("false")) multiplexer_2 (
    .in0(ula_out), .in3(out_6), .out(multiplexer_2_out), .sel(rinctl));  // open: in1, in2, in4, in5, in6, in7
  Registrador registrador_1 (
    .RsX(RsX), .RsY(RsY), .Rd(multiplexer_1_out), .Rin(multiplexer_2_out), .rwctl(rwctl), .R0(R0),
    .Rx(out_6), .Ry(out_7), .clk(clock_1_out));
  Clock clock_1 (.out(clock_1_out));
  \Unidade_Lógica_Aritimética  \unidade_lógica_aritimética_1  (.Ix(out_6), .Iy(out_7), .Op(ula_op), .ula_out(ula_out));

  // Other names for the same wires on the sheet: RX_out[7:0] = out_6; RY_out[7:0] = out_7

  // Notes on the sheet:
  //   UFBa - Universidade Federal da Bahia
  //   Gustavo de Oliveira Ferreia
  //   gust.oliveira.ferreira@gmail.com
  //   BANCO DE REGISTRADORES - REGS
  //   Fase 2.2: União REGs com ULA
endmodule

module IDEC (
  input  [11:0] \INSTRUÇÃO ,
  output [3:0] Op
);


  assign Op = \INSTRUÇÃO [11:8];
endmodule

module CTLU (
  input  [3:0] Op,
  input  R0,
  output rmctl,
  output rwctl,
  output [2:0] rinctl,
  output [1:0] rdctl,
  output wmctl,
  output [1:0] pcctl
);

  wire and_2_out;

  Multiplexer #(.select(4), .enable("false")) multiplexer_1 (
    .in0(1'b0), .in1(1'b0), .in2(1'b0), .in3(1'b0), .in4(1'b0), .in5(1'b0), .in6(1'b0), .in7(1'b0),
    .in8(1'b0), .in9(1'b0), .in10(1'b0), .in11(1'b0), .in12(1'b1), .in13(1'b0), .in14(1'b0), .in15(1'b0),
    .out(rwctl), .sel(Op));
  Multiplexer #(.select(4), .width(3), .enable("false")) multiplexer_2 (
    .in0(3'b000), .in1(3'b000), .in2(3'b000), .in3(3'b000), .in4(3'b000), .in5(3'b000), .in6(3'b000),
    .in7(3'b000), .in8(3'b000), .in9(3'b000), .in10(3'b001), .in11(3'b010), .in12(3'b000), .in13(3'b011),
    .in14(3'b100), .in15(3'b111), .out(rinctl), .sel(Op));
  and and_1 (pcctl[1], Op[3], Op[2], Op[1], ~Op[0], R0);  // AND_Gate
  and and_2 (and_2_out, ~Op[0], ~R0);  // AND_Gate
  Multiplexer #(.select(4), .width(2), .enable("false")) multiplexer_3 (
    .in0(2'b00), .in1(2'b00), .in2(2'b00), .in3(2'b00), .in4(2'b00), .in5(2'b00), .in6(2'b00), .in7(2'b00),
    .in8(2'b00), .in9(2'b00), .in10(2'b00), .in11(2'b00), .in12(2'b10), .in13(2'b10), .in14(2'b01),
    .in15(2'b01), .out(rdctl), .sel(Op));
  or or_1 (pcctl[0], and_2_out, ~Op[3], ~Op[2], ~Op[1]);  // OR_Gate
  Multiplexer #(.select(4), .enable("false")) multiplexer_4 (
    .in0(1'b0), .in1(1'b0), .in2(1'b0), .in3(1'b0), .in4(1'b0), .in5(1'b0), .in6(1'b0), .in7(1'b0),
    .in8(1'b0), .in9(1'b0), .in10(1'b1), .in11(1'b0), .in12(1'b1), .in13(1'b0), .in14(1'b0), .in15(1'b0),
    .out(rmctl), .sel(Op));

  assign wmctl = rmctl;
endmodule

module PC (
  input  [7:0] PC_Adress,
  input  [1:0] pcctl,
  input  PC_clk,
  output [7:0] PC_Out
);

  Counter #(.trigger("falling")) counter_1 (
    .load(pcctl[1]), .D(PC_Adress), .count(pcctl[0]), .Q(PC_Out), .clk(PC_clk));  // open: carry, clr
endmodule

module IR (
  input  [11:0] IR_In,
  input  clk,
  output [11:0] IR_Out
);

  Register #(.width(12)) IR (.D(IR_In), .Q(IR_Out), .clk(clk));  // open: en, clr
endmodule

// Ld/Str
module ld_str_chip (
  input  wmctl,
  input  [3:0] Op,
  output LDA,
  output STR,
  output sel
);

  and and_1 (LDA, Op[3], ~Op[2], Op[1], ~Op[0], wmctl);  // AND_Gate
  and and_2 (STR, Op[3], Op[2], ~Op[1], ~Op[0], wmctl);  // AND_Gate
  or or_1 (sel, STR, LDA);
endmodule

// rinctl
module rinclt_chip (
  input  [7:0] ula_out,
  input  [7:0] dm_out,
  input  [7:0] adress,
  input  [7:0] rinctl_out,
  input  [7:0] pc_out,
  input  [2:0] rinctl,
  output [7:0] rinctl_out_2
);

  Multiplexer #(.select(3), .width(8), .enable("false")) multiplexer_1 (
    .in0(ula_out), .in1(dm_out), .in2(adress), .in3(rinctl_out), .in4(pc_out), .out(rinctl_out_2),
    .sel(rinctl));  // open: in5, in6, in7
endmodule

// rdctl
module rdctl_chip (
  input  [3:0] RsX,
  input  [1:0] rdctl,
  output [3:0] rdctl_out
);

  Multiplexer #(.select(2), .width(4), .enable("false")) multiplexer_1 (
    .in0(4'b0000), .in1(4'b1111), .in2(RsX), .out(rdctl_out), .sel(rdctl));  // open: in3
endmodule

// RsX
module RsX_ctl (
  input  [3:0] RsX,
  input  [3:0] Op,
  output [3:0] RsX_out
);

  wire comparator_1_eq;

  Comparator #(.width(4)) comparator_1 (.a(Op), .b(4'b1100), .eq(comparator_1_eq));  // open: gt, lt
  Multiplexer #(.width(4), .enable("false")) multiplexer_1 (
    .in0(RsX), .in1(4'b0000), .out(RsX_out), .sel(comparator_1_eq));
endmodule
